// Logisim project Clock.circ as structural Verilog: 1 circuit, main circuit main
module main (
);

  wire HB, HC, HD, HE, HF, MA, MB, MC, MD, ME, MF, n6to14_1_p1, n6to14_1_p2, n6to14_1_p3, n6to14_1_p4,
       n6to14_1_p6, n6to14_1_p8, n6to14_1_p10, n6to14_1_p12, n6to14_1_p14, n6to14_1_p16, n6to14_1_p17,
       n6to14_1_p18, n6to14_1_p19, n6to14_1_p20, n6to14_2_p1, n6to14_2_p2, n6to14_2_p3, n6to14_2_p4,
       n6to14_2_p6, n6to14_2_p8, n6to14_2_p10, n6to14_2_p12, n6to14_2_p14, n6to14_2_p16, n6to14_2_p17,
       n6to14_2_p18, n6to14_2_p19, n6to14_2_p20, n6to14_3_p1, n6to14_3_p2, n6to14_3_p3, n6to14_3_p4,
       n6to14_3_p6, n6to14_3_p8, n6to14_3_p10, n6to14_3_p12, n6to14_3_p14, n6to14_3_p16, n6to14_3_p17,
       n6to14_3_p18, n6to14_3_p19, n6to14_3_p20, SA, SB, SC, SD, SE, SF;

  _7_Segment_Display u_7_segment_display_1 (
    .g(n6to14_1_p4), .f(n6to14_1_p2), .a(n6to14_1_p1), .b(n6to14_1_p3), .e(n6to14_1_p6), .d(n6to14_1_p8),
    .c(n6to14_1_p10));  // open: dp
  // _6to14 6to14_1: pin names not known; wires that end beside it: n6to14_1_p1, n6to14_1_p2, n6to14_1_p3, n6to14_1_p4, 1'b0, n6to14_1_p6, HB, n6to14_1_p8, HC, n6to14_1_p10, HD, n6to14_1_p12, HE, n6to14_1_p14, HF, n6to14_1_p16, n6to14_1_p17, n6to14_1_p18, n6to14_1_p19, n6to14_1_p20
  _7_Segment_Display u_7_segment_display_2 (
    .g(n6to14_1_p17), .f(n6to14_1_p14), .a(n6to14_1_p12), .b(n6to14_1_p16), .e(n6to14_1_p18),
    .d(n6to14_1_p19), .c(n6to14_1_p20));  // open: dp
  // Time_main main_1: pin names not known; wires that end beside it: SA, SB, SC, SD, SE, SF, MA, MB, MC, MD, ME, MF, HB, HC, HD, HE, HF
  // _6to14 6to14_2: pin names not known; wires that end beside it: n6to14_2_p1, n6to14_2_p2, n6to14_2_p3, n6to14_2_p4, MA, n6to14_2_p6, MB, n6to14_2_p8, MC, n6to14_2_p10, MD, n6to14_2_p12, ME, n6to14_2_p14, MF, n6to14_2_p16, n6to14_2_p17, n6to14_2_p18, n6to14_2_p19, n6to14_2_p20
  _7_Segment_Display u_7_segment_display_3 (
    .g(n6to14_2_p17), .f(n6to14_2_p14), .a(n6to14_2_p12), .b(n6to14_2_p16), .e(n6to14_2_p18),
    .d(n6to14_2_p19), .c(n6to14_2_p20));  // open: dp
  _7_Segment_Display u_7_segment_display_4 (
    .g(n6to14_2_p4), .f(n6to14_2_p2), .a(n6to14_2_p1), .b(n6to14_2_p3), .e(n6to14_2_p6), .d(n6to14_2_p8),
    .c(n6to14_2_p10));  // open: dp
  _7_Segment_Display u_7_segment_display_5 (
    .g(n6to14_3_p4), .f(n6to14_3_p2), .a(n6to14_3_p1), .b(n6to14_3_p3), .e(n6to14_3_p6), .d(n6to14_3_p8),
    .c(n6to14_3_p10));  // open: dp
  // _6to14 6to14_3: pin names not known; wires that end beside it: n6to14_3_p1, n6to14_3_p2, n6to14_3_p3, n6to14_3_p4, SA, n6to14_3_p6, SB, n6to14_3_p8, SC, n6to14_3_p10, SD, n6to14_3_p12, SE, n6to14_3_p14, SF, n6to14_3_p16, n6to14_3_p17, n6to14_3_p18, n6to14_3_p19, n6to14_3_p20
  _7_Segment_Display u_7_segment_display_6 (
    .g(n6to14_3_p17), .f(n6to14_3_p14), .a(n6to14_3_p12), .b(n6to14_3_p16), .e(n6to14_3_p18),
    .d(n6to14_3_p19), .c(n6to14_3_p20));  // open: dp

  // Notes on the sheet:
  //   Hours
  //   Minutes
  //   Seconds
endmodule
